# Fritzing sketch encoder (saved by Fritzing 0.9.2b)

parts:
  U1 = attiny85 [package=dip]
  P2 = Pushbutton [package=THT]
  P3 = Pushbutton [package=THT]
  10k1 = Resistor [tolerance=±5% resistance=10k package=THT]
  10k2 = Resistor [tolerance=±5% resistance=10k package=THT]
  U2 = mystery part, 2 pins [chip_label=?]
  P4 = Pushbutton [package=THT]
  P5 = Pushbutton [package=THT]
  10k3 = Resistor [tolerance=±5% resistance=10k package=THT]
  10k4 = Resistor [tolerance=±5% resistance=10k package=THT]
  U3 = mystery part, 1 pin [chip_label=?]
  U4 = mystery part, 1 pin [chip_label=?]
  U5 = mystery part, 2 pins [chip_label=?]
  10k5 = Resistor [tolerance=±5% resistance=10k package=THT]
  10k6 = Resistor [tolerance=±5% resistance=10k package=THT]
  Grove1 = Grove OLED 128x96
  U6 = mystery part, 4 pins [chip_label=?]
  SD_card_module2 = SD Card Module
  U7 = mystery part, 4 pins [chip_label=?]
  U8 = mystery part, 4 pins [chip_label=?]

nets:
  N1: U1.Pin_2, P3.leg0, 10k2.Pin_1
  N2: U1.Pin_4, 10k1.Pin_0, 10k2.Pin_0, P4.leg0, P5.leg0, U5.pin2, 10k5.Pin_0, 10k6.Pin_0
  N3: U1.Pin_5, U2.pin2, 10k6.Pin_1
  N4: U1.Pin_6, U2.pin1, 10k5.Pin_1
  N5: U1.Pin_7, P2.leg0, 10k1.Pin_1
  N6: U1.Pin_8, P2.leg1, P3.leg1, 10k3.Pin_1, 10k4.Pin_1, U5.pin1
  N7: P4.leg1, 10k3.Pin_0, U3.pin1
  N8: P5.leg1, 10k4.Pin_0, U4.pin1
  N9: Grove1.GND, U6.pin2
  N10: Grove1.VCC, U6.pin1
  N11: Grove1.SDA, U6.pin3
  N12: Grove1.SCL, U6.pin4
  N13: SD_card_module2.GND, U7.pin1
  N14: SD_card_module2.+5, U7.pin4
  N15: SD_card_module2.CS, U8.pin2
  N16: SD_card_module2.MOSI, U8.pin3
  N17: SD_card_module2.SCK, U7.pin2
  N18: SD_card_module2.MISO, U7.pin3

notes:
  D35
  ^
  v
  MENU/OK
  PARADA EMERGENCIA
  D31
  D41
  10K
  Alimentacion 5V Servo RAMPS
  ENCODER
  21(SCL)
  20(SDA)
  -
  +
  I2C RAMPS
  5V
  MISO
  SCK
  GND
  NC
  D53
  MOSI
  D49
  AUX 3 / SPI RAMPS
  AUX 4 RAMPS
  D37
  LECTOR TARJETAS SD
  PANTALLA OLED 0,96" I2C

custom parts:
  SD Card Module: SD Card Module Slot Socket Reader For Arduino ARM MCU
